# Fritzing sketch Circuit (saved by Fritzing 0.9.3b)
breadboards: 2

parts:
  Part1 = Arduino Uno (Rev3)
  Part2 = Module Bluetooth
  S1 = H-Bridge with L298N
  M1 = DC Motor
  M2 = DC Motor
  VCC1 = Battery block 9V
  M3 = DC Motor
  M4 = DC Motor
  VCC2 = 4 x AAA Battery Mount  # not connected
  VCC3 = 4 x AAA Battery Mount  # not connected
  U1 = SWITCH-SPST-2 [package=switch-spst-vertical]  # not connected
  LED1 = smd LED [color="Red (633nm)" package="0603 [SMD]"]
  LED2 = smd LED [color="Red (633nm)" package="1206 [SMD]"]
  LED3 = smd LED [color="Orange (605nm)" package="1206 [SMD]"]
  LED4 = smd LED [color="Orange (605nm)" package="1206 [SMD]"]
  R1 = Resistor [tolerance=±5% resistance=220 package=THT]
  J1 = Piezo Speaker
  R2 = Resistor [tolerance=±5% resistance=220 package=THT]
  LED5 = LED - 5mm [color="Orange (605nm)" package="5 mm [THT]"]
  LED6 = LED - 5mm [color="Orange (605nm)" package="5 mm [THT]"]
  LED7 = LED - 5mm [color="White (6500K)" package="5 mm [THT]"]
  LED8 = LED - 5mm [color="White (6500K)" package="5 mm [THT]"]
  R3 = Resistor [tolerance=±5% resistance=220 package=THT]
  R4 = Resistor [tolerance=±5% resistance=220 package=THT]

nets:
  N1: Part1.D9_PWM, R2.Pin_0
  N2: Part1.D10_PWM/SS, S1.IN3
  N3: Part1.D11_PWM/MOSI, S1.IN4
  N4: Part1.D12/MISO, R1.Pin_0
  N5: Part1.D13/SCK, R4.Pin_1
  N6: Part1.D0/RX, Part2.TXD
  N7: Part1.D1/TX, Part2.RXD
  N8: Part1.D3_PWM, J1.pin2
  N9: Part1.D5_PWM, S1.IN1
  N10: Part1.D6_PWM, S1.IN2
  5V: Part1.5V, Part2.VCC
  GND: Part1.GND, Part2.GND, S1.GND, VCC1.-
  N11: Part1.VIN, VCC1.+
  N12: S1.ENA, S1.ENA-5V
  N13: S1.ENB, S1.ENB-5V
  N14: S1.M1-01, M1.pin_2
  N15: S1.M1-02, M1.pin_1, M4.pin_1
  N16: S1.M2-01, M2.pin_2, M3.pin_2
  N17: S1.M2-02, M2.pin_1, M3.pin_1
  N18: LED1.cathode, LED2.anode
  N19: LED1.anode, R1.Pin_1
  N20: LED2.cathode, LED4.cathode, J1.pin1
  N21: LED3.cathode, LED4.anode
  N22: LED3.anode, R2.Pin_1
  N23: LED5.cathode, LED7.cathode
  N24: LED5.anode, LED6.cathode
  N25: LED6.anode, R3.Pin_0
  N26: LED7.anode, LED8.cathode
  N27: LED8.anode, R4.Pin_0

custom parts:
  H-Bridge with L298N: h-bridge
